// Logisim project logism电路.circ as structural Verilog: 2 circuits, main circuit led
module led (
  input  x3,
  input  x2,
  input  x1,
  input  x0,
  output a,
  output b,
  output c,
  output d,
  output e,
  output f,
  output g
);

  wire and_1_out, and_2_out, and_3_out, and_4_out, and_5_out, and_6_out, and_7_out, and_8_out, and_9_out,
       and_10_out, and_11_out, and_12_out, and_13_out, and_14_out, and_15_out, and_16_out, and_17_out,
       and_18_out, and_19_out, and_20_out, and_21_out, and_22_out, and_23_out, and_24_out, and_25_out,
       and_26_out, and_27_out, and_28_out, and_29_out, and_30_out, and_31_out, and_32_out, and_33_out,
       and_34_out, and_35_out, not_1_out, not_2_out, not_3_out, not_4_out, not_5_out, not_6_out, not_7_out,
       not_8_out, not_9_out, not_10_out, not_11_out, not_12_out, not_13_out, not_14_out, not_15_out,
       not_16_out, not_17_out, not_18_out, not_19_out, not_20_out, not_21_out, not_22_out, not_23_out,
       not_24_out, not_25_out, not_26_out, not_27_out, not_28_out, not_29_out, not_30_out, not_31_out,
       not_32_out, not_33_out, not_34_out, not_35_out, not_36_out, not_37_out, not_38_out, not_39_out,
       not_40_out, not_41_out, not_42_out, not_43_out;

  not not_1 (not_1_out, x2);
  and and_1 (and_1_out, not_1_out, not_2_out);
  not not_2 (not_2_out, x0);
  not not_3 (not_3_out, x3);
  and and_2 (and_2_out, not_3_out, x1);
  not not_4 (not_4_out, x3);
  and and_3 (and_3_out, not_4_out, x2, x0);
  and and_4 (and_4_out, x2, x1);
  and and_5 (and_5_out, x3, not_5_out, not_6_out);
  not not_5 (not_5_out, x2);
  not not_6 (not_6_out, x1);
  and and_6 (and_6_out, x3, not_7_out);
  not not_7 (not_7_out, x0);
  not not_8 (not_8_out, x1);
  and and_7 (and_7_out, not_8_out, not_9_out);
  not not_9 (not_9_out, x0);
  not not_10 (not_10_out, x3);
  and and_8 (and_8_out, not_10_out, x2, not_11_out);
  not not_11 (not_11_out, x1);
  and and_9 (and_9_out, x2, not_12_out);
  not not_12 (not_12_out, x0);
  and and_10 (and_10_out, x3, not_13_out);
  not not_13 (not_13_out, x2);
  and and_11 (and_11_out, x3, x1);
  not not_14 (not_14_out, x2);
  and and_12 (and_12_out, not_14_out, not_15_out);
  not not_15 (not_15_out, x0);
  and and_13 (and_13_out, x1, not_16_out);
  not not_16 (not_16_out, x0);
  and and_14 (and_14_out, x3, x1);
  and and_15 (and_15_out, x3, x2);
  not not_17 (not_17_out, x3);
  not not_18 (not_18_out, x2);
  and and_16 (and_16_out, not_17_out, not_18_out, not_19_out);
  not not_19 (not_19_out, x0);
  not not_20 (not_20_out, x2);
  and and_17 (and_17_out, not_20_out, x1, x0);
  not not_21 (not_21_out, x1);
  and and_18 (and_18_out, x2, not_21_out, x0);
  and and_19 (and_19_out, x2, x1, not_22_out);
  not not_22 (not_22_out, x0);
  and and_20 (and_20_out, x3, not_23_out);
  not not_23 (not_23_out, x1);
  not not_24 (not_24_out, x3);
  and and_21 (and_21_out, not_24_out, not_25_out);
  not not_25 (not_25_out, x1);
  not not_26 (not_26_out, x3);
  and and_22 (and_22_out, not_26_out, x0);
  not not_27 (not_27_out, x1);
  and and_23 (and_23_out, not_27_out, x0);
  not not_28 (not_28_out, x3);
  and and_24 (and_24_out, not_28_out, x2);
  and and_25 (and_25_out, x3, not_29_out);
  not not_29 (not_29_out, x2);
  not not_30 (not_30_out, x3);
  and and_26 (and_26_out, not_30_out, not_31_out);
  not not_31 (not_31_out, x2);
  not not_32 (not_32_out, x3);
  and and_27 (and_27_out, not_32_out, not_33_out, not_34_out);
  not not_33 (not_33_out, x1);
  not not_34 (not_34_out, x0);
  not not_35 (not_35_out, x2);
  and and_28 (and_28_out, not_35_out, not_36_out);
  not not_36 (not_36_out, x0);
  not not_37 (not_37_out, x3);
  and and_29 (and_29_out, not_37_out, x1, x0);
  and and_30 (and_30_out, x3, not_38_out, x0);
  not not_38 (not_38_out, x1);
  not not_39 (not_39_out, x2);
  and and_31 (and_31_out, not_39_out, x1);
  and and_32 (and_32_out, x1, not_40_out);
  not not_40 (not_40_out, x0);
  not not_41 (not_41_out, x3);
  and and_33 (and_33_out, not_41_out, x2, not_42_out);
  not not_42 (not_42_out, x1);
  and and_34 (and_34_out, x3, not_43_out);
  not not_43 (not_43_out, x2);
  and and_35 (and_35_out, x3, x0);
  or or_1 (b, and_7_out, and_8_out, and_9_out, and_10_out, and_11_out);
  or or_2 (c, and_12_out, and_13_out, and_14_out, and_15_out);
  or or_3 (d, and_16_out, and_17_out, and_18_out, and_19_out, and_20_out);
  or or_4 (e, and_21_out, and_22_out, and_23_out, and_24_out, and_25_out);
  or or_5 (f, and_26_out, and_27_out, and_28_out, and_29_out, and_30_out);
  or or_6 (g, and_31_out, and_32_out, and_33_out, and_34_out, and_35_out);
  or or_7 (a, and_1_out, and_2_out, and_3_out, and_4_out, and_5_out, and_6_out);
  _7_Segment_Display u_7_segment_display_1 (.g(g), .f(b), .a(a), .b(f), .e(c), .d(d), .c(e));  // open: dp
  _7_Segment_Display u_7_segment_display_2 (.e(1'b1));  // open: g, f, a, b, d, c, dp
  _7_Segment_Display u_7_segment_display_3 (.g(1'b1));  // open: f, a, b, e, d, c, dp
  _7_Segment_Display u_7_segment_display_4 (.d(1'b1));  // open: g, f, a, b, e, c, dp
  _7_Segment_Display u_7_segment_display_5 (.f(1'b1));  // open: g, a, b, e, d, c, dp
  _7_Segment_Display u_7_segment_display_6 (.c(1'b1));  // open: g, f, a, b, e, d, dp
  _7_Segment_Display u_7_segment_display_7 (.a(1'b1));  // open: g, f, b, e, d, c, dp
  _7_Segment_Display u_7_segment_display_8 (.dp(1'b1));  // open: g, f, a, b, e, d, c
  _7_Segment_Display u_7_segment_display_9 (.b(1'b1));  // open: g, f, a, e, d, c, dp
endmodule

module led2 (
  input  x0,
  input  x1,
  input  x2,
  input  x3,
  output a,
  output b,
  output c,
  output d,
  output e,
  output f,
  output g
);

  wire and_1_out, and_2_out, and_3_out, and_4_out, and_5_out, and_6_out, and_7_out, and_8_out, and_9_out,
       and_10_out, and_11_out, and_12_out, and_13_out, and_14_out, and_15_out, and_16_out, and_17_out,
       and_18_out, and_19_out, and_20_out, and_21_out, and_22_out, and_23_out, and_24_out, and_25_out,
       and_26_out, and_27_out, and_28_out, and_29_out, and_30_out, and_31_out, and_32_out, and_33_out,
       and_34_out, not_1_out, not_2_out, not_3_out, not_4_out, not_5_out, not_6_out, not_7_out, not_8_out,
       not_9_out, not_10_out, not_11_out, not_12_out, not_13_out, not_14_out, not_15_out, not_16_out,
       not_17_out, not_18_out, not_19_out, not_20_out, not_21_out, not_22_out, not_23_out, not_24_out,
       not_25_out, not_26_out, not_27_out, not_28_out, not_29_out, not_30_out, not_31_out, not_32_out,
       not_33_out, not_34_out, not_35_out, not_36_out, not_37_out, not_38_out, not_39_out, not_40_out,
       not_41_out, not_42_out;

  not not_1 (not_1_out, x1);
  and and_1 (and_1_out, not_1_out, not_2_out);
  not not_2 (not_2_out, x3);
  not not_3 (not_3_out, x0);
  and and_2 (and_2_out, not_3_out, x2);
  not not_4 (not_4_out, x0);
  and and_3 (and_3_out, not_4_out, x1, x3);
  and and_4 (and_4_out, x1, x2);
  not not_5 (not_5_out, x1);
  and and_5 (and_5_out, x0, not_5_out, not_6_out);
  not not_6 (not_6_out, x2);
  and and_6 (and_6_out, x0, not_7_out);
  not not_7 (not_7_out, x3);
  not not_8 (not_8_out, x2);
  and and_7 (and_7_out, not_8_out, not_9_out);
  not not_9 (not_9_out, x3);
  not not_10 (not_10_out, x0);
  and and_8 (and_8_out, not_10_out, x1, not_11_out);
  not not_11 (not_11_out, x2);
  and and_9 (and_9_out, x1, not_12_out);
  not not_12 (not_12_out, x3);
  and and_10 (and_10_out, x0, not_13_out);
  not not_13 (not_13_out, x1);
  and and_11 (and_11_out, x0, x2);
  not not_14 (not_14_out, x1);
  and and_12 (and_12_out, not_14_out, not_15_out);
  not not_15 (not_15_out, x3);
  and and_13 (and_13_out, x2, not_16_out);
  not not_16 (not_16_out, x3);
  and and_14 (and_14_out, x0, x2);
  and and_15 (and_15_out, x0, x1);
  not not_17 (not_17_out, x0);
  and and_16 (and_16_out, not_17_out, not_18_out, not_19_out);
  not not_18 (not_18_out, x1);
  not not_19 (not_19_out, x3);
  not not_20 (not_20_out, x1);
  and and_17 (and_17_out, not_20_out, x2, x3);
  and and_18 (and_18_out, x1, not_21_out, x3);
  not not_21 (not_21_out, x2);
  and and_19 (and_19_out, x1, x2, not_22_out);
  not not_22 (not_22_out, x3);
  and and_20 (and_20_out, x0, not_23_out);
  not not_23 (not_23_out, x2);
  not not_24 (not_24_out, x0);
  and and_21 (and_21_out, not_24_out, not_25_out);
  not not_25 (not_25_out, x2);
  not not_26 (not_26_out, x0);
  and and_22 (and_22_out, not_26_out, x3);
  not not_27 (not_27_out, x2);
  and and_23 (and_23_out, not_27_out, x3);
  not not_28 (not_28_out, x0);
  and and_24 (and_24_out, not_28_out, x1);
  and and_25 (and_25_out, x0, not_29_out);
  not not_29 (not_29_out, x1);
  not not_30 (not_30_out, x0);
  and and_26 (and_26_out, not_30_out, not_31_out);
  not not_31 (not_31_out, x1);
  not not_32 (not_32_out, x0);
  not not_33 (not_33_out, x2);
  and and_27 (and_27_out, not_32_out, not_33_out, not_34_out);
  not not_34 (not_34_out, x3);
  not not_35 (not_35_out, x1);
  and and_28 (and_28_out, not_35_out, not_36_out);
  not not_36 (not_36_out, x3);
  not not_37 (not_37_out, x0);
  and and_29 (and_29_out, not_37_out, x2, x3);
  and and_30 (and_30_out, x0, not_38_out, x3);
  not not_38 (not_38_out, x2);
  not not_39 (not_39_out, x1);
  and and_31 (and_31_out, not_39_out, x2);
  and and_32 (and_32_out, x2, not_40_out);
  not not_40 (not_40_out, x3);
  not not_41 (not_41_out, x0);
  and and_33 (and_33_out, not_41_out, x1, not_42_out);
  not not_42 (not_42_out, x2);
  and and_34 (and_34_out, x0, x3);
  or or_1 (b, and_7_out, and_8_out, and_9_out, and_10_out, and_11_out);
  or or_2 (c, and_12_out, and_13_out, and_14_out, and_15_out);
  or or_3 (d, and_16_out, and_17_out, and_18_out, and_19_out, and_20_out);
  or or_4 (e, and_21_out, and_22_out, and_23_out, and_24_out, and_25_out);
  or or_5 (f, and_26_out, and_27_out, and_28_out, and_29_out, and_30_out);
  or or_6 (g, and_31_out, and_32_out, and_33_out, and_34_out);
  or or_7 (a, and_1_out, and_2_out, and_3_out, and_4_out, and_5_out, and_6_out);
endmodule
