// Logisim project 投票器.circ as structural Verilog: 1 circuit, main circuit vote
module vote (
  input  A,
  input  B,
  input  C,
  output OUT
);

  wire and_1_out, and_2_out, and_3_out;

  and and_1 (and_1_out, B, C);
  and and_2 (and_2_out, A, C);
  and and_3 (and_3_out, A, B);
  or or_1 (OUT, and_1_out, and_2_out, and_3_out);
endmodule
