// Logisim project 第一小题.circ as structural Verilog: 1 circuit, main circuit main
module main (
  input  a0,
  input  a1,
  input  b0,
  input  b1,
  output S0,
  output S1,
  output Carry
);

  wire and_1_out, and_2_out, and_3_out, xor_2_out;

  xor xor_1 (S0, a0, b0);
  and and_1 (and_1_out, a0, b0);
  xor xor_2 (xor_2_out, a1, b1);
  and and_2 (and_2_out, xor_2_out, and_1_out);
  and and_3 (and_3_out, a1, b1);
  xor xor_3 (S1, xor_2_out, and_1_out);
  or or_1 (Carry, and_2_out, and_3_out);
endmodule
