// Logisim project 第二小题.circ as structural Verilog: 1 circuit, main circuit main
module main (
  input  a0,
  input  a1,
  input  b0,
  input  b1,
  input  Cin,
  output S0,
  output S1,
  output Carry
);

  wire and_1_out, and_2_out, and_3_out, and_4_out, xor_1_out, xor_3_out, xor_4_out;

  and and_1 (and_1_out, a0, b0);
  xor xor_1 (xor_1_out, a0, b0);
  and and_2 (and_2_out, Cin, xor_1_out);
  xor xor_2 (S0, xor_1_out, Cin);
  xor xor_3 (xor_3_out, and_1_out, and_2_out);
  xor xor_4 (xor_4_out, a1, b1);
  and and_3 (and_3_out, xor_4_out, xor_3_out);
  and and_4 (and_4_out, a1, b1);
  xor xor_5 (S1, xor_4_out, xor_3_out);
  or or_1 (Carry, and_3_out, and_4_out);
endmodule
